# Fritzing sketch Teensy-Theremin - withoutAudio Shield (saved by Fritzing 0.9.0b)
circuit board: 8.46667cm x 5.64444cm
breadboards: 1

parts:
  R1 = Photocell (LDR) [package=THT]
  R2 = Resistor [tolerance=±5% resistance=220 package=THT]
  Teensy_3_1 = Teensy 3.1  # not connected
  U1 = POT [package=pot_mammoth]
  R3 = Resistor [tolerance=±5% resistance=220 package=THT]
  U2 = POT [package=pot_mammoth]
  R4 = Resistor [tolerance=±5% resistance=220 package=THT]
  Part1 = SRF05 Ultrasonic Rangefinder

nets:
  N1: R1.pin_0, R2.Pin_1
  N2: R1.pin_1, U1.E, U2.E
  N3: R2.Pin_0, R3.Pin_1, R4.Pin_1, Part1.GND
  N4: U1.S, R3.Pin_0
  N5: U2.S, R4.Pin_0

custom parts:
  Teensy 3.1: The Teensy is a complete USB-based microcontoller development system, in a very small footprint, capable of implementing many types of projects. All programming is done via the USB port. No special programmer is needed, only a standard micro-USB cable and a PC or Macintosh with a USB port. It has a USB keyboard/mouse/joystick emulation stack and can be programmed through Arduino IDE.
