# Fritzing sketch Teensy-Theremin5 -2 (saved by Fritzing 0.9.0b)
circuit board: 9.1487cm x 8.12329cm
breadboards: 2

parts:
  LDR = Photocell (LDR) [package=THT]
  R2 = Resistor [tolerance=±5% resistance=10k package=THT]
  U1 = POT [package=pot_mammoth]
  U2 = POT [package=pot_mammoth]
  S2 = Round Pushbutton
  S3 = Round Pushbutton
  S4 = Round Pushbutton
  S5 = Round Pushbutton
  U3 = POT [package=pot_mammoth]
  U4 = POT [package=pot_mammoth]
  R7 = Resistor [tolerance=±5% resistance=10k package=THT]
  R8 = Resistor [tolerance=±5% resistance=10k package=THT]
  HC-SR04 = HC-SR04 Ultrasonic rangefinder
  JP1 = M16 [package=1x16_machine-pin-header_lock.004]
  JP2 = M16 [package=1x16_machine-pin-header_lock.004]
  R10 = Resistor [tolerance=±5% resistance=10k package=THT]
  R9 = Resistor [tolerance=±5% resistance=10k package=THT]

nets:
  N1: LDR.pin_0, R2.Pin_1, JP2.7
  N2: LDR.pin_1, U1.E, U2.E, S2.leg1, S3.leg1, S4.leg1, S5.leg1, U3.E, U4.E, JP2.3
  N3: R2.Pin_0, U1.S, U2.S, U3.S, U4.S, R7.Pin_1, R8.Pin_1, HC-SR04.GND, JP1.1, R10.Pin_1, R9.Pin_1
  N4: U1.A, JP2.6
  N5: U2.A, JP2.10
  N6: S2.leg0, R7.Pin_0, JP1.4
  N7: S3.leg0, R8.Pin_0, JP1.5
  N8: S4.leg0, JP1.6, R9.Pin_0
  N9: S5.leg0, JP1.7, R10.Pin_0
  N10: U3.A, JP2.11
  N11: U4.A, JP2.12
  N12: HC-SR04.VCC, JP2.1
  N13: HC-SR04.Trig, JP1.2
  N14: HC-SR04.Echo, JP1.3
