# Fritzing sketch Teensy-Theremin5 -3 (saved by Fritzing 0.9.0b)
circuit board: 10.9497cm x 9.9625cm
breadboards: 2

parts:
  LDR = Photocell (LDR) [package=THT]
  R2 = Resistor [tolerance=±5% resistance=10k package=THT]
  U1 = POT [package=pot_mammoth]
  U2 = POT [package=pot_mammoth]
  S2 = Round Pushbutton
  S3 = Round Pushbutton
  S4 = Round Pushbutton
  S5 = Round Pushbutton
  U3 = POT [package=pot_mammoth]
  U4 = POT [package=pot_mammoth]
  R7 = Resistor [tolerance=±5% resistance=10k package=THT]
  R8 = Resistor [tolerance=±5% resistance=10k package=THT]
  HC-SR04 = HC-SR04 Ultrasonic rangefinder
  R10 = Resistor [tolerance=±5% resistance=10k package=THT]
  R9 = Resistor [tolerance=±5% resistance=10k package=THT]
  J1 = female pin header, 14 pins [form="♀ (female)"]
  J2 = female pin header, 14 pins [form="♀ (female)"]
  Teensy_3_1 = Teensy 3.1

nets:
  N1: LDR.pin_0, R2.Pin_1, J1.pin7
  N2: LDR.pin_1, U1.E, U2.E, S2.leg1, S3.leg1, S4.leg1, S5.leg1, U3.E, U4.E, J1.pin3
  GND: R2.Pin_0, U1.S, U2.S, U3.S, U4.S, R7.Pin_1, R8.Pin_1, HC-SR04.GND, R10.Pin_1, R9.Pin_1, J2.pin1, Teensy_3_1.GND
  N3: U1.A, J1.pin6
  N4: U2.A, J1.pin10
  N5: S2.leg0, R7.Pin_0, J2.pin4
  N6: S3.leg0, R8.Pin_0, J2.pin5
  N7: S4.leg0, R9.Pin_0, J2.pin6
  N8: S5.leg0, R10.Pin_0, J2.pin7
  N9: U3.A, J1.pin11
  N10: U4.A, J1.pin12
  N11: HC-SR04.VCC, J1.pin1
  N12: HC-SR04.Trig, J2.pin2
  N13: HC-SR04.Echo, J2.pin3

notes:
  KonkaSynth
