# Fritzing sketch WavPlayerPlusPlus (saved by Fritzing 0.9.0b)
circuit board: 8.46667cm x 5.64444cm
breadboards: 1

parts:
  Teensy_3_1 = Teensy 3.1
  S1 = Pushbutton [package="[THT]"]
  R1 = Resistor [tolerance=±5% resistance=220 package=THT]

nets:
  N1: Teensy_3_1.GND, R1.Pin_1
  N2: Teensy_3_1.D0, S1.Pin_3, S1.Pin_4, R1.Pin_0
  N3: Teensy_3_1.Vin, S1.Pin_1, S1.Pin_2
